// Logisim project 55189 (AND, OR, NOT, XOR, NAND, NOR, HALF ADDER, FULL ADDER).circ as structural Verilog: 1 circuit, main circuit main
module main (
  input  in_1,
  input  in_2,
  input  in_3,
  input  in_4,
  input  in_5,
  input  in_6,
  input  in_7,
  input  in_8,
  input  in_9,
  input  in_10,
  input  in_11,
  input  in_12,
  input  in_13,
  input  in_14,
  input  in_15,
  input  in_16
);

  wire and_1_out, and_2_out, and_3_out, and_4_out, and_5_out, and_6_out, and_7_out, and_8_out, and_9_out,
       and_10_out, not_1_out, not_2_out, not_3_out, not_4_out, not_5_out, not_6_out, not_7_out, or_1_out,
       or_2_out, or_3_out, or_4_out, or_5_out, or_6_out;

  not not_1 (not_1_out, in_13);
  not not_2 (not_2_out, in_12);
  not not_3 (not_3_out, in_7);
  not not_4 (not_4_out, in_6);
  and and_1 (and_1_out, in_14, in_15);
  and and_2 (and_2_out, in_15, in_16);
  and and_3 (and_3_out, in_16, in_14);
  and and_4 (and_4_out, in_1, in_2);
  not not_5 (not_5_out, in_3);
  or or_1 (or_1_out, in_4, in_5);
  and and_5 (and_5_out, in_6, not_3_out);
  and and_6 (and_6_out, not_4_out, in_7);
  and and_7 (and_7_out, in_8, in_9);
  or or_2 (or_2_out, in_10, in_11);
  and and_8 (and_8_out, in_12, not_1_out);
  and and_9 (and_9_out, not_2_out, in_13);
  LED led_1 (.in(and_10_out));
  and and_10 (and_10_out, in_12, in_13);
  LED led_2 (.in(and_4_out));
  LED led_3 (.in(not_5_out));
  LED led_4 (.in(or_1_out));
  or or_3 (or_3_out, and_5_out, and_6_out);
  not not_6 (not_6_out, and_7_out);
  not not_7 (not_7_out, or_2_out);
  or or_4 (or_4_out, and_8_out, and_9_out);
  or or_5 (or_5_out, in_14, in_15, in_16);
  LED led_5 (.in(or_3_out));
  LED led_6 (.in(not_6_out));
  LED led_7 (.in(not_7_out));
  LED led_8 (.in(or_4_out));
  LED led_9 (.in(or_5_out));
  or or_6 (or_6_out, and_1_out, and_2_out, and_3_out);
  LED led_10 (.in(or_6_out));

  // Notes on the sheet:
  //   NAND GATE
  //   NOR GATE
  //   HALF ADDER
  //   Full Adder
  //   AND GATE
  //   NOT GATE
  //   OR GATE
  //   XOR GATE
endmodule
