// Logisim project Encoder.circ as structural Verilog: 1 circuit, main circuit main
module main (
  input  D9,
  input  D8,
  input  D7,
  input  D6,
  input  D5,
  input  D4,
  input  D3,
  input  D2,
  input  D1
);

  wire or_1_out, or_2_out, or_3_out, or_4_out;

  or or_1 (or_1_out, D1, D3, D5, D7, D9);
  LED led_1 (.in(or_1_out));
  or or_2 (or_2_out, D2, D3, D6, D7);
  LED led_2 (.in(or_2_out));
  or or_3 (or_3_out, D4, D5, D6, D7);
  LED led_3 (.in(or_3_out));
  LED led_4 (.in(or_4_out));
  or or_4 (or_4_out, D8, D9);

  // Notes on the sheet:
  //   Encoder
  //   Y0
  //   Y1
  //   Y2
  //   Y3
endmodule
